# Fritzing sketch connections_pc (saved by Fritzing 0.9.4)

parts:
  Composant1 = Arduino Pro Micro (Clone)
  Composant2 = 24 NeoPixel Ring [part_number=1586]
  R3 = Resistor [tolerance=±5% resistance=330 package=THT]
  KY-1 = Keyes Relay [package=THT]
  TSOP = TSOP312.., 314.. [part_number=1556 package=THT]
  R4 = Resistor [tolerance=±5% resistance=330 package=THT]
  C2 = Electrolytic Capacitor [capacitance=1000µF package="300 mil [THT, electrolytic]"]
  RESET = Pushbutton [package="[THT]"]
  R3_2 = Resistor [tolerance=±5% resistance=330 package="0603 [SMD]"]
  R4_2 = Resistor [tolerance=±5% resistance=330 package="0603 [SMD]"]
  LED2_+_R2_330Ω = LED - 3mm [color="Blue (470nm)" package="3 mm [THT]"]
  LED1_+_R1_330Ω = LED - 3mm [color="Red (635nm)" package="3 mm [THT]"]
  Power_plug2 = Power plug
  R0 = Resistor [tolerance=±5% resistance=330 package="0603 [SMD]"]
  LED_FOR_TEST_ON_PC = LED - 3mm [color="Green (565nm)" package="3 mm [THT]"]

nets:
  GND: Composant1.GND, Composant2.GND, KY-1.ground, TSOP.GND, C2.-, RESET.Pin_1, RESET.Pin_2, LED2_+_R2_330Ω.cathode, LED1_+_R1_330Ω.cathode, Power_plug2.GND, LED_FOR_TEST_ON_PC.cathode
  N1: Composant1.D2, RESET.Pin_4
  N2: Composant1.D6, R4_2.Pin_1
  N3: Composant1.D7, KY-1.signal
  N4: Composant1.D9, R3_2.Pin_1
  N5: Composant1.D10, R3.Pin_1
  N6: Composant1.A2, R4.Pin_1
  N7: Composant1.VCC, KY-1.power, KY-1.C, TSOP.Vs
  N8: Composant2.IN, R3.Pin_0
  VDD: Composant2.VDD, C2.+, Power_plug2.VCC
  N9: KY-1.NO, R0.Pin_1
  N10: TSOP.Data, R4.Pin_0
  N11: R3_2.Pin_0, LED2_+_R2_330Ω.anode
  N12: R4_2.Pin_0, LED1_+_R1_330Ω.anode
  N13: R0.Pin_0, LED_FOR_TEST_ON_PC.anode

notes:
  Power Supply
  5v (2+ Amps)
  Connect a Micro USB cable between the Pro Micro and the PC

custom parts:
  24 NeoPixel Ring: 24 ultra bright smart LED NeoPixels are arranged in a circle with 2.6" (66mm) outer diameter. The rings are 'chainable' - connect the output pin of one to the input pin of another. Use only one microcontroller pin to control as many as you can chain together! Each LED is addressable as the driver chip is inside the LED. Each one has ~18mA constant current drive so the color will be very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
  Keyes Relay: The Keyes 5V relay module is suitable for SCM development, home appliance control. It uses a 5V~12V TIL control signal which can control DC / AC signal.
  TSOP312.., 314..: The TSOP312.., TSOP314.. series are miniaturized receivers for infrared remote control systems. A PIN diode and a preamplifier are assembled on a lead frame, the epoxy package acts as an IR filter. The demodulated output signal can be directly decoded by a microprocessor. The TSOP312.. is compatible with all common IR remote control data formats. The TSOP314.. is optimized to suppress almost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
