# Fritzing sketch connections_xbox (saved by Fritzing 0.9.4)

parts:
  Composant1 = Arduino Pro Micro (Clone)
  Composant2 = 24 NeoPixel Ring [part_number=1586]
  R3 = Resistor [tolerance=±5% resistance=330 package=THT]
  KY-1 = Keyes Relay [package=THT]
  TSOP = TSOP312.., 314.. [part_number=1556 package=THT]
  R4 = Resistor [tolerance=±5% resistance=330 package=THT]
  SW2_(Xbox_front_Panel) = Pushbutton [package="[THT]"]
  Mod1 = generic-ac-power-supply [package=THT]
  JP3 = USB_MICROB_PLUG [package=micro-b-ra-th]
  C2 = Electrolytic Capacitor [capacitance=1000µF package="300 mil [THT, electrolytic]"]
  JP6 = Header 1 [package=1x01_offset]
  JP7 = Header 1 [package=1x01_offset]
  RESET = Pushbutton [package="[THT]"]
  R3_2 = Resistor [tolerance=±5% resistance=330 package="0603 [SMD]"]
  R4_2 = Resistor [tolerance=±5% resistance=330 package="0603 [SMD]"]
  LED2_+_R2_330Ω = LED - 3mm [color="Blue (470nm)" package="3 mm [THT]"]
  LED1_+_R1_330Ω = LED - 3mm [color="Red (635nm)" package="3 mm [THT]"]
  PSU_CONNECTOR = ATX24 Pin Power Supply Connector [package=atx24_right_angle]  # not connected
  <3_LFRAME4 = molex pin header, 1 pin [form=molex]
  <3_LFRAME5 = molex pin header, 1 pin [form=molex]
  <3_LFRAME6 = molex pin header, 1 pin [form=molex]
  R5_-_R7 = Resistor [tolerance=±5% resistance=10k package=THT]
  3_3v_*_(R6_/_(R5+R6))_=_1_65v1 = Resistor [tolerance=±5% resistance=10k package=THT]

nets:
  GND: Composant1.GND, Composant2.GND, KY-1.ground, TSOP.GND, C2.-, RESET.Pin_1, RESET.Pin_2, LED2_+_R2_330Ω.cathode, LED1_+_R1_330Ω.cathode, <3_LFRAME5.pin1, 3_3v_*_(R6_/_(R5+R6))_=_1_65v1.Pin_0
  N1: Composant1.D2, RESET.Pin_4
  N2: Composant1.D6, R4_2.Pin_1
  N3: Composant1.D7, KY-1.signal
  N4: Composant1.D9, R3_2.Pin_1
  N5: Composant1.D10, R3.Pin_1
  N6: Composant1.A0, R5_-_R7.Pin_1, 3_3v_*_(R6_/_(R5+R6))_=_1_65v1.Pin_1
  N7: Composant1.A2, R4.Pin_1
  N8: Composant1.VCC, KY-1.power, TSOP.Vs
  N9: Composant2.IN, R3.Pin_0
  N10: Composant2.VDD, C2.+, <3_LFRAME4.pin1
  N11: KY-1.C, SW2_(Xbox_front_Panel).Pin_2
  N12: KY-1.NO, SW2_(Xbox_front_Panel).Pin_4
  N13: TSOP.Data, R4.Pin_0
  N14: Mod1.pin1, JP7.1
  N15: Mod1.pin2, JP6.1
  N16: Mod1.pin3#2, JP3.VCC
  N17: Mod1.pin3#3, JP3.D+
  N18: R3_2.Pin_0, LED2_+_R2_330Ω.anode
  N19: R4_2.Pin_0, LED1_+_R1_330Ω.anode
  N20: <3_LFRAME6.pin1, R5_-_R7.Pin_0

notes:
  AC 120v
  AC 230v
  to
  DC 5.0v
  XBOX
  FRONT

custom parts:
  24 NeoPixel Ring: 24 ultra bright smart LED NeoPixels are arranged in a circle with 2.6" (66mm) outer diameter. The rings are 'chainable' - connect the output pin of one to the input pin of another. Use only one microcontroller pin to control as many as you can chain together! Each LED is addressable as the driver chip is inside the LED. Each one has ~18mA constant current drive so the color will be very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
  Keyes Relay: The Keyes 5V relay module is suitable for SCM development, home appliance control. It uses a 5V~12V TIL control signal which can control DC / AC signal.
  TSOP312.., 314..: The TSOP312.., TSOP314.. series are miniaturized receivers for infrared remote control systems. A PIN diode and a preamplifier are assembled on a lead frame, the epoxy package acts as an IR filter. The demodulated output signal can be directly decoded by a microprocessor. The TSOP312.. is compatible with all common IR remote control data formats. The TSOP314.. is optimized to suppress almost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
  generic-ac-power-supply: Generic ac power supply module. Use as is, or customize the svgs to fit your particular device (as they are all different.) Provides AC input and single DC output. PCB is generic and will need modifications if you intend to do a pcb mount.
