# Fritzing sketch debugTsop (saved by Fritzing 0.9.4)

parts:
  TSOP1 = TSOP312.., 314.. [part_number=1556 package=THT]
  Composant1 = Arduino Pro Micro (Clone)
  R1 = Resistor [tolerance=±5% resistance=330 package=THT]

nets:
  GND: TSOP1.GND, Composant1.GND
  N1: TSOP1.Vs, Composant1.VCC
  N2: TSOP1.Data, R1.Pin_1
  N3: Composant1.A2, R1.Pin_0

notes:
  Connect a Micro USB cable between the Pro Micro and the PC

custom parts:
  TSOP312.., 314..: The TSOP312.., TSOP314.. series are miniaturized receivers for infrared remote control systems. A PIN diode and a preamplifier are assembled on a lead frame, the epoxy package acts as an IR filter. The demodulated output signal can be directly decoded by a microprocessor. The TSOP312.. is compatible with all common IR remote control data formats. The TSOP314.. is optimized to suppress almost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
