# Fritzing sketch multiple (saved by Fritzing 0.9.4)

parts:
  <_1 = 24 NeoPixel Ring [part_number=1586]
  Composant4 = NeoPixel Stick [part_number=1426]
  Composant5 = NeoPixel Stick [part_number=1426]
  Composant6 = NeoPixel Stick [part_number=1426]
  Composant7 = NeoPixel Stick [part_number=1426]
  Composant8 = NeoPixel Stick [part_number=1426]
  Composant9 = NeoPixel Stick [part_number=1426]
  Composant10 = NeoPixel Stick [part_number=1426]
  Composant11 = NeoPixel Stick [part_number=1426]
  Composant13 = NeoPixel Stick [part_number=1426]
  25_> = NeoPixel Stick [part_number=1426]
  132_> = NeoPixel Stick [part_number=1426]
  Composant15 = NeoPixel Stick [part_number=1426]
  Composant16 = NeoPixel Stick [part_number=1426]
  Composant17 = NeoPixel Stick [part_number=1426]
  Composant18 = Arduino Pro Micro (Clone)
  R1 = Resistor [tolerance=±5% resistance=330 package=THT]
  C3 = Electrolytic Capacitor [capacitance=1000µF package="300 mil [THT, electrolytic]"]
  Power_plug3 = Power plug
  Power_plug4 = Power plug
  C4 = Electrolytic Capacitor [capacitance=1000µF package="300 mil [THT, electrolytic]"]

nets:
  N1: <_1.IN, R1.Pin_0
  N2: <_1.OUT, 25_>.DATAOUT
  GND: <_1.GND, Composant4.GND, Composant5.GND, Composant6.GND, Composant7.GND, Composant8.GND, Composant9.GND, Composant10.GND, Composant11.GND, Composant13.GND, 25_>.GND, 132_>.GND, Composant15.GND, Composant16.GND, Composant17.GND, Power_plug4.GND, C4.-
  +5V: <_1.VDD, Composant4.+5V, Composant5.+5V, Composant6.+5V, Composant7.+5V, Composant8.+5V, Composant15.+5V, Composant17.+5V, Power_plug4.VCC, C4.+
  N3: Composant4.DATAOUT, Composant6.DATAIN
  N4: Composant4.DATAIN, Composant15.DATAOUT
  N5: Composant5.DATAOUT, Composant15.DATAIN
  N6: Composant5.DATAIN, Composant8.DATAOUT
  N7: Composant6.DATAOUT, Composant9.DATAIN
  N8: Composant7.DATAOUT, Composant17.DATAIN
  N9: Composant7.DATAIN, Composant13.DATAOUT
  N10: Composant8.DATAIN, Composant17.DATAOUT
  N11: Composant9.DATAOUT, Composant16.DATAIN
  +5V_2: Composant9.+5V, Composant10.+5V, Composant11.+5V, Composant16.+5V, C3.+, Power_plug3.VCC
  N12: Composant10.DATAOUT, Composant11.DATAIN
  N13: Composant10.DATAIN, Composant16.DATAOUT
  +5V_3: Composant13.+5V, 25_>.+5V, 132_>.+5V
  N14: Composant13.DATAIN, 132_>.DATAOUT
  N15: Composant18.D10, R1.Pin_1
  N16: C3.-, Power_plug3.GND

notes:
  Only connect GND and DATA between strips

custom parts:
  24 NeoPixel Ring: 24 ultra bright smart LED NeoPixels are arranged in a circle with 2.6" (66mm) outer diameter. The rings are 'chainable' - connect the output pin of one to the input pin of another. Use only one microcontroller pin to control as many as you can chain together! Each LED is addressable as the driver chip is inside the LED. Each one has ~18mA constant current drive so the color will be very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
  NeoPixel Stick: Make your own little LED strip arrangement with this stick of NeoPixel LEDs. We crammed 8 of the tiny 5050 (5mm x 5mm) smart RGB LEDs onto a PCB with mounting holes and a chainable design. Use only one microcontroller pin to control as many as you can chain together! Each LED is addressable as the driver chip is inside the LED. Each one has ~18mA constant current drive so the color will be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
